# Fritzing sketch fritz_project (saved by Fritzing 0.9.3b)
breadboards: 1

parts:
  Часть1 = Arduino Nano (Rev3.0)
  L298N1 = L298N DC motor driver
  ZS-042_RTC1 = ZS-042 RTC Module
  R1 = Resistor [tolerance=±5% resistance=220 package=THT]
  LED1 = LED - 5mm [color="Red (633nm)" package="5 mm [THT]"]

nets:
  GND: Часть1.GND, L298N1.GND, ZS-042_RTC1.GND, R1.Pin_1
  N1: Часть1.D4, LED1.anode
  N2: Часть1.D5, L298N1.IN1
  N3: Часть1.D6, L298N1.IN2
  5V: Часть1.5V, L298N1.5V#7, ZS-042_RTC1.VCC
  N4: Часть1.A5, ZS-042_RTC1.SCL
  N5: Часть1.A4, ZS-042_RTC1.SDA
  N6: L298N1.5V#9, L298N1.ENA
  N7: L298N1.5V#10, L298N1.ENB
  N8: R1.Pin_0, LED1.cathode

custom parts:
  L298N DC motor driver: 2x DC motor driver with 78M05 positive voltage regulator (7..35 V) L298N: max 46 V, 2 A Set 5 V Enable jumper to enable 5 V regultor (needed for the L298N) and +5 V output at screw terminal or supply external +5 V at screw terminal Set ENA and/or ENB to +5 V to enable motor permanently or supply ENA and/or ENB with PWM signal IN1 and IN2 set rotation directory for motor A (OUT1/OUT2) IN2 and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
